# Fritzing sketch full_schematic (saved by Fritzing 0.9.3b)
breadboards: 2

parts:
  Aduino_Uno = Arduino Uno (Rev3)
  U1 = MCP4725 [package=SOT23-6]
  Q1 = NPN-Transistor [package="TO92 [THT]"]
  J1 = Piezo Speaker
  LED2 = LED - 5mm [color="Green (555nm)" package="5 mm [THT]"]
  LED1 = RGB LED (com. cathode, rbg) [package="5 mm [THT]"]
  BioRay_Laser = mystery part, 1 pin [chip_label=?]
  R1 = Resistor [tolerance=±5% resistance=2.2k package=THT]
  Manta_Camera = mystery part, 4 pins [chip_label=?]
  R2 = Resistor [tolerance=±5% resistance=2.2k package=THT]
  Raspberry_Pi_3_B+ = Raspberry Pi 3 [part_number=RPI-3-V1.2]
  U3 = 74*32 [package=sot353]
  Safety_Interlock = mystery part, 1 pin [chip_label=ILOCK]
  R3 = Resistor [tolerance=±5% resistance=2.2k package=THT]
  Interlock_override = Tilt Switch [package=THT]
  R4 = Resistor [tolerance=±5% resistance=2.2k package=THT]

nets:
  N1: Aduino_Uno.A0, Raspberry_Pi_3_B+.GPIO16
  N2: Aduino_Uno.A1, Raspberry_Pi_3_B+.GPIO26
  N3: Aduino_Uno.A2, Raspberry_Pi_3_B+.GPIO23, U3.A, Safety_Interlock.pin1, R3.Pin_1
  N4: Aduino_Uno.A3, Raspberry_Pi_3_B+.GPIO24, U3.B, Interlock_override.Pin_2, R4.Pin_1
  N5: Aduino_Uno.A4/SDA, U1.SDA
  N6: Aduino_Uno.A5/SCL, U1.SCL
  N7: Aduino_Uno.D8, Raspberry_Pi_3_B+.GPIO17
  N8: Aduino_Uno.D9_PWM, LED1.green_anode
  N9: Aduino_Uno.D10_PWM/SS, LED1.blue_anode
  N10: Aduino_Uno.D11_PWM/MOSI, LED1.red_anode
  N11: Aduino_Uno.D2, R1.Pin_1, Manta_Camera.pin3
  N12: Aduino_Uno.D3_PWM, Manta_Camera.pin1
  N13: Aduino_Uno.D4, Raspberry_Pi_3_B+.GPIO22
  N14: Aduino_Uno.D5_PWM, LED2.anode
  N15: Aduino_Uno.D6_PWM, J1.pin2
  N16: Aduino_Uno.D7, Raspberry_Pi_3_B+.GPIO27
  N17: Aduino_Uno.RESET, Q1.E
  5V: Aduino_Uno.5V, Manta_Camera.pin4, U3.VCC
  GND: Aduino_Uno.GND, U1.VSS, Q1.C, J1.pin1, LED2.cathode, LED1.common_cathode, R1.Pin_0, Manta_Camera.pin2, U3.GND, R3.Pin_0, Interlock_override.Pin_1, R4.Pin_0
  N18: U1.VDD, U3.Y
  N19: U1.VOUT, BioRay_Laser.pin1
  N20: Q1.B, R2.Pin_0
  N21: R2.Pin_1, Raspberry_Pi_3_B+.GPIO25
